# Fritzing sketch fritzingµ (saved by Fritzing 0.9.4)
breadboards: 1

parts:
  Onderdeel1 = Arduino Micro (Rev3)  # not connected
  J1 = Basic Servo
  J2 = Basic Servo
  Pololu_A1 = Pololu A4988 [package=SO16]
  Raspberry_Pi_1 = Raspberry Pi 3 [part_number=RPI-3-V1.2]  # not connected
  M1 = DC Motor
  M2 = DC Motor
  BAT1 = Battery Holders [package=lipo-1100mAh]

nets:
  GND: J1.gnd, J2.gnd, Pololu_A1.ENABLE, Pololu_A1.MS3, Pololu_A1.RESET, BAT1.-
  VCC: J1.vcc, J2.vcc, BAT1.+
  N1: Pololu_A1.1B, M2.pin_2
  N2: Pololu_A1.1A, M2.pin_1
  N3: Pololu_A1.2A, M1.pin_2
  N4: Pololu_A1.2B, M1.pin_1

notes:
  5V 1500mAh LIPO
  Camera is mounted on holder which moves using these two servos]
  PiCam is used
